# Fritzing sketch Private_Chat_Room (saved by Fritzing 0.9.3b)
breadboards: 2

parts:
  Matrix_keypad1 = KEYPAD 4x4
  U1 = NodeMCU V1.0
  Part1 = LED Tactile Button Breakout v10 [part_number=BOB-10467]

nets:
  N1: Matrix_keypad1.col1, U1.D7
  N2: Matrix_keypad1.col2, U1.D6
  N3: Matrix_keypad1.col3, U1.D5
  N4: Matrix_keypad1.col4, U1.D4
  N5: Matrix_keypad1.row1, U1.D3
  N6: Matrix_keypad1.row2, U1.D2
  N7: Matrix_keypad1.row3, U1.D1
  N8: Matrix_keypad1.row4, U1.D0
  N9: U1.3V3, Part1.4
  N10: U1.GND, Part1.3
  N11: U1.D8, Part1.1

notes:
  NodeMCU [ESP-12E]
  8 LED 4X4 Keypad with Buttons

custom parts:
  KEYPAD 4x4: Matrix keypad 16 buttons, 4 rows x 4 columns
  NodeMCU V1.0: ESP8266 based NodeMCU
